// Logisim project BeEight.circ as structural Verilog: 4 circuits, main circuit main
module main (
  input  in_1,
  input  D0,
  input  RESET,
  input  D1,
  input  HLT,
  input  D2,
  input  RES,
  input  D3,
  output [11:0] Address
);

  wire adder_2_cout, ALUD0, ALUD1, ALUD2, ALUD3, ALUD4, ALUD5, ALUD6, ALUD7, and_1_out, and_2_out, and_3_out,
       and_4_out, and_5_out, and_6_out, and_8_out, and_9_out, and_10_out, and_11_out, and_12_out, and_13_out,
       and_14_out, and_18_out, and_19_out, Carry, CLK, CLKIN, Cond0, Cond1, Cond2, Cond3, ConditionalFlag,
       ConditionalResult, controlled_buffer_9_out, controlled_buffer_12_out, controlled_buffer_13_out,
       controlled_buffer_14_out, controlled_buffer_15_out, controlled_buffer_16_out,
       controlled_buffer_17_out, controlled_buffer_18_out, Equal, GreaterThan, ia, ialu, im, inone, Inst0,
       Inst1, Inst2, Inst3, ipb, ipc, ipcs, isb, LessThan, n74138_1_pin4, n74138_1_pin5, n74138_1_pin6,
       n74138_2_pin4, n74138_2_pin5, n74138_2_pin6, n74138_3_pin4, n74138_3_pin5, n74138_3_pin6,
       n74138_3_pin7, n74138_3_pin9, n74138_3_pin10, n74138_3_pin11, n74138_3_pin12, n74138_3_pin13,
       n74138_3_pin14, n74138_3_pin15, n74161_1_pin7, n74161_1_pin10, n74161_1_pin15, n74161_2_pin7,
       n74161_2_pin15, n74161_3_pin7, n74161_4_pin1, n74161_4_pin2, n74161_4_pin7, n74161_4_pin9,
       n74161_4_pin10, nor_1_out, not_1_out, not_2_out, not_3_out, not_5_out, not_6_out, not_7_out,
       not_8_out, not_9_out, not_10_out, not_11_out, not_12_out, not_13_out, not_14_out, not_15_out,
       not_16_out, not_17_out, not_20_out, not_21_out, not_22_out, not_23_out, not_24_out, not_25_out,
       not_26_out, not_28_out, not_29_out, not_30_out, not_31_out, not_32_out, not_33_out, not_34_out,
       not_35_out, not_36_out, not_37_out, not_38_out, nxt, oa, oalu, om, onone, opb, opc, opcs, or_1_out,
       or_2_out, or_3_out, or_4_out, or_5_out, osb, PB4, PB5, PB6, PB7, pull_resistor_5_node,
       pull_resistor_6_node, pull_resistor_7_node, pull_resistor_8_node, pull_resistor_9_node,
       pull_resistor_10_node, pull_resistor_18_node, RESET_t, s_r_ff_1_qn, special, ucf;
  wire [3:0] DatabusUpper, InstructionCounter;
  wire [6:0] rom_1_data;
  wire [7:0] Accumulator, Accumulator_q, adder_1_out, adder_2_out, ALU, Databus, nand_1_out, not_27_out,
       PrimaryBuffer, SecondaryBuffer;
  wire [7:4] octaldtypelatchoe_1_q;
  wire [11:0] StoredAddress;

  not not_1 (not_1_out, special);
  or or_1 (or_1_out, opcs, not_1_out);
  QuadBusBuffers quadbusbuffers_1 (
    .nG1(or_1_out), .A1(DatabusUpper[0]), .nG2(or_1_out), .A2(DatabusUpper[1]), .nG3(or_1_out),
    .A3(DatabusUpper[2]), .nG4(or_1_out), .A4(DatabusUpper[3]), .Y1(Databus[0]), .Y2(Databus[1]),
    .Y3(Databus[2]), .Y4(Databus[3]));
  Pull_Resistor pull_resistor_1 (.node(Databus[4]));
  Pull_Resistor pull_resistor_2 (.node(Databus[5]));
  Pull_Resistor pull_resistor_3 (.node(Databus[6]));
  Pull_Resistor pull_resistor_4 (.node(Databus[7]));
  Hex_Digit_Display #(.decimalPoint("false")) hex_digit_display_1 (.value(Address[11:8]));
  Hex_Digit_Display #(.decimalPoint("false")) hex_digit_display_2 (.value({Inst3, Inst2, Inst1, Inst0}));
  Hex_Digit_Display #(.decimalPoint("false")) hex_digit_display_3 (.value(InstructionCounter));
  or or_2 (or_2_out, opcs, special);
  Hex_Digit_Display #(.decimalPoint("false")) hex_digit_display_4 (.value(Address[7:4]));
  Hex_Digit_Display #(.decimalPoint("false")) hex_digit_display_5 (.value(Address[3:0]));
  Hex_Digit_Display #(.decimalPoint("false")) hex_digit_display_6 (.value(DatabusUpper));
  Hex_Digit_Display #(.decimalPoint("false")) hex_digit_display_7 (.value(Databus[7:4]));
  not not_2 (not_2_out, im);
  and and_1 (and_1_out, not_2_out, CLK);
  QuadBusBuffers quadbusbuffers_2 ();  // open: nG1, A1, nG2, A2, nG3, A3, nG4, A4, Y1, Y2, Y3, Y4
  Hex_Digit_Display #(.decimalPoint("false")) hex_digit_display_8 (.value(Accumulator[7:4]));
  Hex_Digit_Display #(.decimalPoint("false")) hex_digit_display_9 (.value(Accumulator[3:0]));
  Hex_Digit_Display #(.decimalPoint("false")) hex_digit_display_10 (.value(Databus[3:0]));
  not not_3 (not_3_out, om);
  OctalDTypeLatchOE ProgramCounterStorageLower (
    .D0(Databus[0]), .D1(Databus[1]), .D2(Databus[2]), .D3(Databus[3]), .D4(Databus[4]), .D5(Databus[5]),
    .D6(Databus[6]), .CK(and_2_out), .nOE(or_2_out), .D7(Databus[7]), .Q0(Databus[0]), .Q1(Databus[1]),
    .Q2(Databus[2]), .Q3(Databus[3]), .Q4(Databus[4]), .Q5(Databus[5]), .Q6(Databus[6]), .Q7(Databus[7]),
    .Q(StoredAddress[7:0]));
  and and_2 (and_2_out, CLK, not_5_out);
  OctalDTypeLatchOE octaldtypelatchoe_1 (
    .D0(DatabusUpper[0]), .D1(DatabusUpper[1]), .D2(DatabusUpper[2]), .D3(DatabusUpper[3]),
    .D4(pull_resistor_8_node), .D5(pull_resistor_7_node), .D6(pull_resistor_6_node), .CK(and_3_out),
    .nOE(or_2_out), .D7(pull_resistor_5_node), .Q0(DatabusUpper[0]), .Q1(DatabusUpper[1]),
    .Q2(DatabusUpper[2]), .Q3(DatabusUpper[3]), .Q({octaldtypelatchoe_1_q, StoredAddress[11:8]}));  // open: Q4, Q5, Q6, Q7
  Pull_Resistor pull_resistor_5 (.node(pull_resistor_5_node));
  Pull_Resistor pull_resistor_6 (.node(pull_resistor_6_node));
  Pull_Resistor pull_resistor_7 (.node(pull_resistor_7_node));
  Pull_Resistor pull_resistor_8 (.node(pull_resistor_8_node));
  and and_3 (and_3_out, CLK, not_6_out);
  Hex_Digit_Display #(.decimalPoint("false")) hex_digit_display_11 (.value(ALU[7:4]));
  Hex_Digit_Display #(.decimalPoint("false")) hex_digit_display_12 (.value(PrimaryBuffer[7:4]));
  Hex_Digit_Display #(.decimalPoint("false")) hex_digit_display_13 (.value(PrimaryBuffer[3:0]));
  not not_4 (RESET_t, RESET);
  Clock u_CLK (.out(CLKIN));
  RAM #(.addrWidth(12), .databus("bidir"), .trigger("high"), .\type ("nonvolatile")) ram_1 (
    .addr(Address), .we(and_1_out), .oe(not_3_out), .data(Databus));
  not not_5 (not_5_out, ipcs);
  not not_6 (not_6_out, ipcs);
  LED led_1 (.in(onone));
  LED led_2 (.in(inone));
  Hex_Digit_Display #(.decimalPoint("false")) hex_digit_display_14 (.value(ALU[3:0]));
  Hex_Digit_Display #(.decimalPoint("false")) hex_digit_display_15 (.value(SecondaryBuffer[7:4]));
  Hex_Digit_Display #(.decimalPoint("false")) hex_digit_display_16 (.value(SecondaryBuffer[3:0]));
  LED led_3 (.in(om));
  LED led_4 (.in(opb));
  LED led_5 (.in(im));
  LED led_6 (.in(ipb));
  Hex_Digit_Display #(.decimalPoint("false")) hex_digit_display_17 (.value(StoredAddress[11:8]));
  Hex_Digit_Display #(.decimalPoint("false")) hex_digit_display_18 (.value(StoredAddress[7:4]));
  not not_7 (not_7_out, special);
  assign {PB7, PB6, PB5, PB4} = special ? {Inst3, Inst2, Inst1, Inst0} : 4'bz;  // Controlled_Buffer controlled_buffer_1
  LED led_7 (.in(osb));
  LED led_8 (.in(oa));
  LED led_9 (.in(isb));
  LED led_10 (.in(ia));
  Hex_Digit_Display #(.decimalPoint("false")) hex_digit_display_19 (.value(StoredAddress[3:0]));
  not not_8 (not_8_out, osb);
  and and_4 (and_4_out, not_8_out, Inst0, Inst1, Inst2);
  assign {PB7, PB6, PB5, PB4} = not_7_out ? Databus[7:4] : 4'bz;  // Controlled_Buffer controlled_buffer_2
  LED led_11 (.in(oalu));
  LED led_12 (.in(opc));
  LED led_13 (.in(ialu));
  LED led_14 (.in(ipc));
  LED led_15 (.in(special));
  LED led_16 (.in(CLK));
  LED led_17 (.in(nxt));
  LED led_18 (.in(ConditionalFlag));
  LED RD (.in(om));
  LED WR (.in(im));
  not not_9 (not_9_out, and_4_out);
  and and_5 (and_5_out, and_4_out, ConditionalFlag);
  LED led_19 (.in(opcs));
  LED led_20 (.in(ipcs));
  or or_3 (or_3_out, not_9_out, and_5_out);
  not not_10 (not_10_out, ipc);
  and and_6 (and_6_out, CLK, or_3_out, not_10_out);
  S_R_Flip_Flop s_r_ff_1 (.reset(RES), .Qn(s_r_ff_1_qn), .preset(HLT));  // open: S, R, clk, Q
  assign DatabusUpper = not_11_out ? {Cond3, Cond2, Cond1, Cond0} : 4'bz;  // Controlled_Buffer controlled_buffer_3
  not not_11 (not_11_out, osb);
  and and_7 (CLK, s_r_ff_1_qn, CLKIN);
  OctalDTypeLatchOE u_PrimaryBuffer (
    .D0(Databus[0]), .D1(Databus[1]), .D2(Databus[2]), .D3(Databus[3]), .D4(PB4), .D5(PB5), .D6(PB6),
    .CK(and_8_out), .nOE(1'b0), .D7(PB7), .Q0(Cond0), .Q1(Cond1), .Q2(Cond2), .Q3(Cond3), .Q4(Inst0),
    .Q5(Inst1), .Q6(Inst2), .Q7(Inst3), .Q(PrimaryBuffer));
  and and_8 (and_8_out, CLK, not_12_out);
  OctalDTypeLatchOE u_SecondaryBuffer (
    .D0(Databus[0]), .D1(Databus[1]), .D2(Databus[2]), .D3(Databus[3]), .D4(Databus[4]), .D5(Databus[5]),
    .D6(Databus[6]), .CK(and_9_out), .nOE(osb), .D7(Databus[7]), .Q0(Databus[0]), .Q1(Databus[1]),
    .Q2(Databus[2]), .Q3(Databus[3]), .Q4(Databus[4]), .Q5(Databus[5]), .Q6(Databus[6]), .Q7(Databus[7]),
    .Q(SecondaryBuffer));
  and and_9 (and_9_out, CLK, not_13_out);
  _74161 #(.ShowInternalStructure("true")) u_74161_1 (
    .pin1(RESET_t), .pin2(and_6_out), .pin3(Databus[0]), .pin4(Databus[1]), .pin5(Databus[2]),
    .pin6(Databus[3]), .pin7(n74161_1_pin7), .pin15(n74161_1_pin15), .pin14(Address[0]), .pin13(Address[1]),
    .pin12(Address[2]), .pin11(Address[3]), .pin10(n74161_1_pin10), .pin9(special));
  _74161 #(.ShowInternalStructure("true")) u_74161_2 (
    .pin1(RESET_t), .pin2(and_6_out), .pin3(Databus[4]), .pin4(Databus[5]), .pin5(Databus[6]),
    .pin6(Databus[7]), .pin7(n74161_2_pin7), .pin15(n74161_2_pin15), .pin14(Address[4]), .pin13(Address[5]),
    .pin12(Address[6]), .pin11(Address[7]), .pin10(n74161_1_pin15), .pin9(special));
  _74161 #(.ShowInternalStructure("true")) u_74161_3 (
    .pin1(RESET_t), .pin2(and_6_out), .pin3(DatabusUpper[0]), .pin4(DatabusUpper[1]), .pin5(DatabusUpper[2]),
    .pin6(DatabusUpper[3]), .pin7(n74161_3_pin7), .pin14(Address[8]), .pin13(Address[9]),
    .pin12(Address[10]), .pin11(Address[11]), .pin10(n74161_2_pin15), .pin9(special));  // open: pin15
  not not_12 (not_12_out, ipb);
  not not_13 (not_13_out, isb);
  Adder adder_1 (.a(Accumulator), .b(Databus), .out(adder_1_out), .cin(ConditionalFlag), .cout(Carry));
  _74283 #(.ShowInternalStructure("true")) u_74283_1 ();  // open: pin1, pin2, pin3, pin4, pin5, pin6, pin7, pin15, pin14, pin13, pin12, pin11, pin10, pin9
  not not_14 (not_14_out, RESET_t);
  or or_4 (or_4_out, not_14_out, nxt);
  assign {DatabusUpper, Databus} = not_15_out ? Address : 12'bz;  // Controlled_Buffer controlled_buffer_4
  not not_15 (not_15_out, opc);
  not not_16 (not_16_out, Inst3);
  not not_17 (not_17_out, Cond0);
  and and_10 (and_10_out, not_16_out, Cond0, Inst0);
  and and_11 (and_11_out, not_16_out, not_17_out, Inst0);
  assign nand_1_out = ~(Accumulator & Databus);  // NAND_Gate nand_1, 8 bits wide
  assign {ALUD7, ALUD6, ALUD5, ALUD4, ALUD3, ALUD2, ALUD1, ALUD0} = and_10_out ? {ConditionalFlag, Accumulator[7:1]} : 8'bz;  // Controlled_Buffer controlled_buffer_5
  _74161 #(.ShowInternalStructure("true")) u_74161_4 (
    .pin1(n74161_4_pin1), .pin2(n74161_4_pin2), .pin7(n74161_4_pin7), .pin14(InstructionCounter[0]),
    .pin13(InstructionCounter[1]), .pin12(InstructionCounter[2]), .pin11(InstructionCounter[3]),
    .pin10(n74161_4_pin10), .pin9(n74161_4_pin9));  // open: pin3, pin4, pin5, pin6, pin15
  not not_18 (n74161_4_pin1, or_4_out);
  not not_19 (n74161_4_pin2, CLK);
  and and_12 (and_12_out, Inst3, Inst0);
  assign {ALUD7, ALUD6, ALUD5, ALUD4, ALUD3, ALUD2, ALUD1, ALUD0} = and_12_out ? nand_1_out : 8'bz;  // Controlled_Buffer controlled_buffer_6
  assign {ALUD7, ALUD6, ALUD5, ALUD4, ALUD3, ALUD2, ALUD1, ALUD0} = and_11_out ? {Accumulator[6:0], ConditionalFlag} : 8'bz;  // Controlled_Buffer controlled_buffer_7
  not not_20 (not_20_out, Inst0);
  assign {ALUD7, ALUD6, ALUD5, ALUD4, ALUD3, ALUD2, ALUD1, ALUD0} = not_20_out ? adder_1_out : 8'bz;  // Controlled_Buffer controlled_buffer_8
  ROM rom_1 (
    .addr({Inst3, Inst2, Inst1, Inst0, InstructionCounter}),
    .data({nxt, rom_1_data[6:4], special, rom_1_data[2:0]}));
  // Probe on Accumulator_q
  OctalDTypeLatchOE u_Accumulator (
    .D0(Databus[0]), .D1(Databus[1]), .D2(Databus[2]), .D3(Databus[3]), .D4(Databus[4]), .D5(Databus[5]),
    .D6(Databus[6]), .CK(and_13_out), .nOE(1'b0), .D7(Databus[7]), .Q0(Accumulator[0]), .Q1(Accumulator[1]),
    .Q2(Accumulator[2]), .Q3(Accumulator[3]), .Q4(Accumulator[4]), .Q5(Accumulator[5]), .Q6(Accumulator[6]),
    .Q7(Accumulator[7]), .Q(Accumulator_q));
  OctalDTypeLatchOE ALUBuffer (
    .D0(ALUD0), .D1(ALUD1), .D2(ALUD2), .D3(ALUD3), .D4(ALUD4), .D5(ALUD5), .D6(ALUD6), .CK(and_14_out),
    .nOE(oalu), .D7(ALUD7), .Q0(Databus[0]), .Q1(Databus[1]), .Q2(Databus[2]), .Q3(Databus[3]),
    .Q4(Databus[4]), .Q5(Databus[5]), .Q6(Databus[6]), .Q7(Databus[7]), .Q(ALU));
  and and_13 (and_13_out, CLK, not_21_out);
  not not_21 (not_21_out, ia);
  and and_14 (and_14_out, CLK, not_22_out);
  not not_22 (not_22_out, ialu);
  assign controlled_buffer_9_out = not_23_out ? Carry : 1'bz;  // Controlled_Buffer controlled_buffer_9
  not not_23 (not_23_out, ucf);
  assign controlled_buffer_9_out = ucf ? ConditionalResult : 1'bz;  // Controlled_Buffer controlled_buffer_10
  _74138 #(.ShowInternalStructure("true")) u_74138_1 (
    .pin1(rom_1_data[0]), .pin2(rom_1_data[1]), .pin3(rom_1_data[2]), .pin4(n74138_1_pin4),
    .pin5(n74138_1_pin5), .pin6(n74138_1_pin6), .pin7(ipcs), .pin15(inone), .pin14(im), .pin13(ipb),
    .pin12(isb), .pin11(ia), .pin10(ialu), .pin9(ipc));
  _74138 #(.ShowInternalStructure("true")) u_74138_2 (
    .pin1(rom_1_data[4]), .pin2(rom_1_data[5]), .pin3(rom_1_data[6]), .pin4(n74138_2_pin4),
    .pin5(n74138_2_pin5), .pin6(n74138_2_pin6), .pin7(opcs), .pin15(onone), .pin14(om), .pin13(opb),
    .pin12(osb), .pin11(oa), .pin10(oalu), .pin9(opc));
  assign Databus = not_24_out ? Accumulator : 8'bz;  // Controlled_Buffer controlled_buffer_11
  not not_24 (not_24_out, oa);
  not not_25 (not_25_out, ialu);
  Register #(.width(1)) register_1 (
    .D(controlled_buffer_9_out), .en(not_25_out), .clk(CLK), .Q(ConditionalFlag));  // open: clr
  not not_26 (not_26_out, ialu);
  and and_15 (ucf, not_26_out, special);
  assign not_27_out = ~Accumulator;  // NOT_Gate not_27, 8 bits wide
  Pull_Resistor #(.pull(1)) pull_resistor_9 (.node(pull_resistor_9_node));
  Adder adder_2 (.a(Databus), .b(not_27_out), .out(adder_2_out), .cin(pull_resistor_9_node), .cout(adder_2_cout));
  _74138 #(.ShowInternalStructure("true")) u_74138_3 (
    .pin1(Cond1), .pin2(Cond2), .pin3(Cond3), .pin4(n74138_3_pin4), .pin5(n74138_3_pin5),
    .pin6(n74138_3_pin6), .pin7(n74138_3_pin7), .pin15(n74138_3_pin15), .pin14(n74138_3_pin14),
    .pin13(n74138_3_pin13), .pin12(n74138_3_pin12), .pin11(n74138_3_pin11), .pin10(n74138_3_pin10),
    .pin9(n74138_3_pin9));
  nor nor_1 (nor_1_out, adder_2_out[0], adder_2_out[1], adder_2_out[2], adder_2_out[3], adder_2_out[4], adder_2_out[5], adder_2_out[6], adder_2_out[7]);
  not not_28 (not_28_out, nor_1_out);
  not not_29 (not_29_out, n74138_3_pin15);
  Pull_Resistor pull_resistor_10 (.node(pull_resistor_10_node));
  assign controlled_buffer_12_out = not_29_out ? pull_resistor_10_node : 1'bz;  // Controlled_Buffer controlled_buffer_12
  not not_30 (not_30_out, n74138_3_pin14);
  assign controlled_buffer_13_out = not_30_out ? Equal : 1'bz;  // Controlled_Buffer controlled_buffer_13
  not not_31 (not_31_out, n74138_3_pin13);
  assign controlled_buffer_14_out = not_31_out ? LessThan : 1'bz;  // Controlled_Buffer controlled_buffer_14
  and and_16 (Equal, nor_1_out, adder_2_cout);
  and and_17 (LessThan, adder_2_cout, not_28_out);
  nor nor_2 (GreaterThan, Equal, LessThan);
  not not_32 (not_32_out, n74138_3_pin12);
  assign controlled_buffer_15_out = not_32_out ? GreaterThan : 1'bz;  // Controlled_Buffer controlled_buffer_15
  not not_33 (not_33_out, n74138_3_pin11);
  assign controlled_buffer_16_out = not_33_out ? D0 : 1'bz;  // Controlled_Buffer controlled_buffer_16
  not not_34 (not_34_out, n74138_3_pin10);
  assign controlled_buffer_17_out = not_34_out ? D1 : 1'bz;  // Controlled_Buffer controlled_buffer_17
  not not_35 (not_35_out, n74138_3_pin9);
  assign controlled_buffer_18_out = not_35_out ? D2 : 1'bz;  // Controlled_Buffer controlled_buffer_18
  Pull_Resistor pull_resistor_11 (.node(controlled_buffer_12_out));
  Pull_Resistor pull_resistor_12 (.node(controlled_buffer_13_out));
  Pull_Resistor pull_resistor_13 (.node(controlled_buffer_14_out));
  Pull_Resistor pull_resistor_14 (.node(controlled_buffer_15_out));
  Pull_Resistor pull_resistor_15 (.node(controlled_buffer_16_out));
  Pull_Resistor pull_resistor_16 (.node(controlled_buffer_17_out));
  Pull_Resistor pull_resistor_17 (.node(controlled_buffer_18_out));
  not not_36 (not_36_out, n74138_3_pin7);
  Pull_Resistor pull_resistor_18 (.node(pull_resistor_18_node));
  assign pull_resistor_18_node = not_36_out ? D3 : 1'bz;  // Controlled_Buffer controlled_buffer_19
  or or_5 (or_5_out, controlled_buffer_12_out, controlled_buffer_13_out, controlled_buffer_14_out, controlled_buffer_15_out, controlled_buffer_16_out, controlled_buffer_17_out, controlled_buffer_18_out, pull_resistor_18_node);
  and and_18 (and_18_out, ucf, Cond0);
  not not_37 (not_37_out, or_5_out);
  assign ConditionalResult = and_18_out ? not_37_out : 1'bz;  // Controlled_Buffer controlled_buffer_20
  assign ConditionalResult = and_19_out ? or_5_out : 1'bz;  // Controlled_Buffer controlled_buffer_21
  and and_19 (and_19_out, ucf, not_38_out);
  Pull_Resistor pull_resistor_19 (.node(ConditionalResult));
  not not_38 (not_38_out, Cond0);
  // also tied to GND on the sheet: {n74138_1_pin4, n74138_1_pin5, n74138_2_pin4, n74138_2_pin5, n74138_3_pin4, n74138_3_pin5}
  // also tied to VCC on the sheet: {n74161_1_pin7, n74161_2_pin7, n74161_3_pin7, n74161_1_pin10, n74161_4_pin7, n74161_4_pin10, n74161_4_pin9, n74138_1_pin6, n74138_2_pin6, n74138_3_pin6}

  // Other names for the same wires on the sheet: AQ1 = Accumulator[1]; AQ2 = Accumulator[2]; AQ3 = Accumulator[3];
  //   AQ4 = Accumulator[4]; AQ5 = Accumulator[5]; AQ6 = Accumulator[6]; AQ7 = Accumulator[7]; DB0 = Databus[0];
  //   Memory[7:0] = Databus; PB0 = Databus[0]; DB1 = Databus[1]; PB1 = Databus[1]; DB2 = Databus[2]; PB2 = Databus[2];
  //   DB3 = Databus[3]; PB3 = Databus[3]; DB4 = Databus[4]; DB5 = Databus[5]; DB6 = Databus[6]; DB7 = Databus[7];
  //   DB8 = DatabusUpper[0]; DB9 = DatabusUpper[1]; DB10 = DatabusUpper[2]; DB11 = DatabusUpper[3];
  //   Instruction[3:0] = {Inst3, Inst2, Inst1, Inst0}; AQ0 = Accumulator[0];
  //   ALUin[7:0] = {ALUD7, ALUD6, ALUD5, ALUD4, ALUD3, ALUD2, ALUD1, ALUD0};
  //   Condition[3:0] = {Cond3, Cond2, Cond1, Cond0}; Dev0 = D0; Dev1 = D1; Dev2 = D2; Dev3 = D3; HALT = HLT

  // Notes on the sheet:
  //   SL
  //   SR
  //   contents of rom_1 (hex, n*v repeats v):
  //   12 e 14 e 80 11*0 12 e 13 e 67 36 41 76 80 7*0 12 e 13 e 35 54 80 9*0 12 e 5 54 80 11*0 12 e 1d e 80
  //   11*0 12 e 13 e 67 36 79 e 71 76 80 5*0 12 e 13 36 80 11*0 12 e 13 e 36 80 10*0 12 e 13 e 67 36 14 76
  //   80 7*0 12 e 13 e 67 36 1a e 13 36 41 76 80 0 0 0 12 e 13 e 67 36 13 35 54 76 80 5*0 12 e 13 e 13 35
  //   54 80 8*0 12 5d e 80 12*0 12 e 13 e 67 36 1a e 13 36 79 e 71 76 80 0 12 e 13 36 1a e 13 36 80 7*0 12
  //   e 13 36 1a e 13 36 80
  //   This is basically a Multiplexer
endmodule

module OctalDTypeLatchOE (
  input  D0,
  input  D1,
  input  D2,
  input  D3,
  input  D4,
  input  D5,
  input  D6,
  input  D7,
  input  CK,
  input  nOE,
  output [7:0] Q,
  output Q0,
  output Q1,
  output Q2,
  output Q3,
  output Q4,
  output Q5,
  output Q6,
  output Q7
);

  wire d_ff_1_qn, d_ff_2_qn, d_ff_3_qn, d_ff_4_qn, d_ff_5_qn, d_ff_6_qn, d_ff_7_qn, d_ff_8_qn, not_1_out,
       not_2_out, not_3_out;

  D_Flip_Flop d_ff_1 (.D(D0), .clk(not_2_out), .Q(Q[0]), .Qn(d_ff_1_qn));  // open: preset, reset
  not not_1 (not_1_out, CK);
  not not_2 (not_2_out, not_1_out);
  not not_3 (not_3_out, nOE);
  D_Flip_Flop d_ff_2 (.D(D1), .clk(not_2_out), .Q(Q[1]), .Qn(d_ff_2_qn));  // open: preset, reset
  assign Q0 = not_3_out ? ~d_ff_1_qn : 1'bz;  // Controlled_Inverter controlled_inverter_1
  D_Flip_Flop d_ff_3 (.D(D2), .clk(not_2_out), .Q(Q[2]), .Qn(d_ff_3_qn));  // open: preset, reset
  assign Q1 = not_3_out ? ~d_ff_2_qn : 1'bz;  // Controlled_Inverter controlled_inverter_2
  D_Flip_Flop d_ff_4 (.D(D3), .clk(not_2_out), .Q(Q[3]), .Qn(d_ff_4_qn));  // open: preset, reset
  assign Q2 = not_3_out ? ~d_ff_3_qn : 1'bz;  // Controlled_Inverter controlled_inverter_3
  D_Flip_Flop d_ff_5 (.D(D4), .clk(not_2_out), .Q(Q[4]), .Qn(d_ff_5_qn));  // open: preset, reset
  assign Q3 = not_3_out ? ~d_ff_4_qn : 1'bz;  // Controlled_Inverter controlled_inverter_4
  D_Flip_Flop d_ff_6 (.D(D5), .clk(not_2_out), .Q(Q[5]), .Qn(d_ff_6_qn));  // open: preset, reset
  assign Q4 = not_3_out ? ~d_ff_5_qn : 1'bz;  // Controlled_Inverter controlled_inverter_5
  D_Flip_Flop d_ff_7 (.D(D6), .clk(not_2_out), .Q(Q[6]), .Qn(d_ff_7_qn));  // open: preset, reset
  assign Q5 = not_3_out ? ~d_ff_6_qn : 1'bz;  // Controlled_Inverter controlled_inverter_6
  D_Flip_Flop d_ff_8 (.D(D7), .clk(not_2_out), .Q(Q[7]), .Qn(d_ff_8_qn));  // open: preset, reset
  assign Q6 = not_3_out ? ~d_ff_7_qn : 1'bz;  // Controlled_Inverter controlled_inverter_7
  assign Q7 = not_3_out ? ~d_ff_8_qn : 1'bz;  // Controlled_Inverter controlled_inverter_8
endmodule

module extTest (
);

  main main_1 ();  // open: in_1, D0, RESET, D1, HLT, D2, RES, D3, Address
endmodule

module QuadBusBuffers (
  input  nG1,
  input  A1,
  input  nG2,
  input  A2,
  input  nG3,
  input  A3,
  input  nG4,
  input  A4,
  output Y1,
  output Y2,
  output Y3,
  output Y4
);

  wire not_1_out, not_2_out, not_3_out, not_4_out;

  not not_1 (not_1_out, nG1);
  assign Y1 = not_1_out ? A1 : 1'bz;  // Controlled_Buffer controlled_buffer_1
  not not_2 (not_2_out, nG2);
  assign Y2 = not_2_out ? A2 : 1'bz;  // Controlled_Buffer controlled_buffer_2
  not not_3 (not_3_out, nG3);
  assign Y3 = not_3_out ? A3 : 1'bz;  // Controlled_Buffer controlled_buffer_3
  not not_4 (not_4_out, nG4);
  assign Y4 = not_4_out ? A4 : 1'bz;  // Controlled_Buffer controlled_buffer_4
endmodule
